# Fritzing sketch BALLANDPLATE (saved by Fritzing 1.0.3b)

parts:
  M1 = DOIT Esp32 DevKit v1 (30 pins long, 11 pins width) [part_number=ESP32S-PIN30]
  LCD1 = 1_54in tft lcd
  Componente2 = RAMPS 1.4 Shield for Arduino Mega 2560
  Componente3 = Black Joystick KY-023
  DRV_3 = DRV 8825 Stepper Motor Carrier, High Current [part_number="DRV 8825"]  # not connected
  DRV_4 = DRV 8825 Stepper Motor Carrier, High Current [part_number="DRV 8825"]  # not connected
  DRV_5 = DRV 8825 Stepper Motor Carrier, High Current [part_number="DRV 8825"]  # not connected
  M2 = Stepper Motor - Bipolar  # not connected
  M3 = Stepper Motor - Bipolar  # not connected
  M4 = Stepper Motor - Bipolar  # not connected
  Enc1 = AMT103
  Enc2 = AMT103
  Enc3 = AMT103
  A1 = DFR0379
  JACK1 = 2.1mm Barrel Jack with Terminal Block
  S1 = Toggle Switch [package=THT]
  J1 = Screw terminal - 2 pins [package=THT]
  J2 = Screw terminal - 2 pins [package=THT]
  J3 = Screw terminal - 2 pins [package=THT]
  J4 = Screw terminal - 2 pins [package=THT]
  J5 = Camdenboss CTB0158-4 [part_number=CTB0158-4 package=THT]

nets:
  3V3: M1.3V3, LCD1.pin2, LCD1.pin_8, Componente3.+5V
  GND: M1.GND, LCD1.pin_1, Componente2.GND/AUX3, Componente2.GND/SERVO#395, Componente3.GND
  N1: M1.D2, LCD1.pin_6
  N2: M1.D4, LCD1.pin_5
  N3: M1.D5, Componente2.D53/AUX3
  N4: M1.D18, Componente2.D52/SCK/AUX3
  N5: M1.D19, Componente2.D50/MISO/AUX3
  N6: M1.D23, Componente2.D51/MOSI/AUX3
  N7: M1.D34, Componente3.VRx
  N8: M1.D35, Componente3.VRy
  N9: M1.D33, Componente3.SW
  N10: M1.D25, LCD1.pin_7
  N11: M1.D26, LCD1.pin4
  N12: M1.D27, LCD1.pin3
  N13: M1.VIN, S1.COM
  N14: Componente2.D64/A10, J5.pin3
  N15: Componente2.D65/A11, J5.pin1
  N16: Componente2.D66/A12, J5.pin2
  N17: Componente2.D59/A5, J5.pin4
  N18: Componente2.D21/SCL, Enc1.B
  N19: Componente2.D20/SDA, Enc1.A
  N20: Componente2.D19/ZMAX_ENDSTOP, Enc2.B
  N21: Componente2.D18/ZMIN_ENDSTOP, Enc2.A
  N22: Componente2.GND/AUX1A, Componente2.GND/AUX1B, Componente2.GND/TEMP_2, Componente2.5A-, A1.Pin_3, A1.Pin_4, A1.Pin_5, A1.Pin_6, JACK1.NEG
  N23: Componente2.D3/XMIN_ENDSTOP, Enc3.A
  N24: Componente2.5A+, A1.Pin_2, JACK1.POS
  N25: Componente2.GND/XMAX_ENDSTOP, Componente2.GND/ZMAX_ENDSTOP
  N26: Componente2.GND/SERVO#396, J4.pin1
  N27: Componente2.D2/XMAX_ENDSTOP, Enc3.B
  N28: Componente2.5V_SERVO#400, A1.Pin_7
  N29: Componente2.5V_SERVO#401, S1.L1
  N30: Componente2.5V_SERVO#402, J4.pin2
  N31: Enc1.5V, J3.pin2
  N32: Enc1.GND, J3.pin1
  N33: Enc2.5V, J2.pin2
  N34: Enc2.GND, J2.pin1
  N35: Enc3.5V, J1.pin2
  N36: Enc3.GND, J1.pin1

notes:
  Encoder X
  Encoder Y
  Encoder Z
  Motor X
  Motor Y
  Motor Z
  12V DC
  A
  Touch

custom parts:
  DOIT Esp32 DevKit v1 (30 pins long, 11 pins width): The DOIT Esp32 DevKit v1 is one of the development board created by DOIT to evaluate the ESP-WROOM-32 module. It is based on the ESP32 microcontroller that boasts Wifi, Bluetooth, Ethernet and Low Power support all in a single chip. (vanepp) made breadboard work, adjusted pin numbering and labels and reduced size of schematic and cleaned up pcb. This chip is 30pins long (2 x15) and 11 pins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
  1_54in tft lcd: This is the DONGKER 1.54'' LCD Display Module, SPI 240x240 1.54'' LCD Display Module ST7789 Driver 240x240 3.3V IPS LCD Display Screen Module. The 1.54" display has 240x240 color pixels.
  RAMPS 1.4 Shield for Arduino Mega 2560: This ia standard Ramps 1.4 shield which is also compatible with versions 1.5 and 1.6 of the Ramps board. This model is intended only for the breadboard view, as the schematic and PCB views are not entirely accurate.
  Black Joystick KY-023: Description: The joystick is a combination of 2 analoog potentiometer and a digital switch. Arduino GND --> Module pin - Arduino +5V --> Module pin +5V Arduino Analoog 0 --> Module VRx Arduino Analoog 1 --> Module VRy Arduino Digital --> Module SW Dimensions: 1" x 1.25"
  AMT103: CUI AMT103 Modular incremental encoder. Resolutions 48, 96, 100, 125, 192, 200, 250, 256, 384, 400, 500, 512, 800, 1000, 1024, 2048 either fixed (resolution indicated by part number) or selectable via dip switch. Index output once per revolution. VCC 5V (3.6V min, probably too high for 3.3V operation)
  DFR0379: 20W Adjustable DC-DC Buck Converter with Digital Display.
